# Fritzing sketch Random_Number_Generator_Circuit_2 (saved by Fritzing 0.9.3b)
breadboards: 1

parts:
  Part1 = Arduino Uno (Rev3)
  LED1 = LED - 5mm [color="Green (570nm)" package="5 mm [THT]"]
  LED2 = LED - 5mm [color="Green (570nm)" package="5 mm [THT]"]
  LED3 = LED - 5mm [color="Yellow (595nm)" package="5 mm [THT]"]
  LED4 = LED - 5mm [color="Yellow (595nm)" package="5 mm [THT]"]
  LED5 = LED - 5mm [color="Red (633nm)" package="5 mm [THT]"]
  LED6 = LED - 5mm [color="Red (633nm)" package="5 mm [THT]"]
  R1 = Resistor [tolerance=±20% resistance=100 package=THT]
  R2 = Resistor [tolerance=±20% resistance=100 package=THT]
  R3 = Resistor [tolerance=±20% resistance=100 package=THT]
  R4 = Resistor [tolerance=±20% resistance=100 package=THT]
  R5 = Resistor [tolerance=±20% resistance=100 package=THT]
  R6 = Resistor [tolerance=±20% resistance=10k package=THT]
  S1 = Pushbutton [package="[THT]"]
  R7 = Resistor [tolerance=±20% resistance=100 package=THT]

nets:
  N1: Part1.D8, R7.Pin_0
  N2: Part1.D9_PWM, R5.Pin_0
  N3: Part1.D10_PWM/SS, R4.Pin_0
  N4: Part1.D11_PWM/MOSI, R3.Pin_0
  N5: Part1.D12/MISO, R2.Pin_0
  N6: Part1.D13/SCK, R1.Pin_0
  N7: Part1.D7, R6.Pin_0, S1.Pin_1, S1.Pin_2
  N8: Part1.5V, S1.Pin_3, S1.Pin_4
  N9: Part1.GND, LED1.cathode, LED2.cathode, LED3.cathode, LED4.cathode, LED5.cathode, LED6.cathode, R6.Pin_1
  N10: LED1.anode, R1.Pin_1
  N11: LED2.anode, R2.Pin_1
  N12: LED3.anode, R3.Pin_1
  N13: LED4.anode, R4.Pin_1
  N14: LED5.anode, R5.Pin_1
  N15: LED6.anode, R7.Pin_1
